# Fritzing sketch Wiring (saved by Fritzing 1.0.4)
breadboards: 1

parts:
  Bauteil1 = LCD1602-I2C
  Bauteil2 = Arduino Nano (Rev3.0)
  RE1 = KY-040 Rotary encoder [package=THT]

nets:
  GND: Bauteil1.GND, Bauteil2.GND, RE1.GND
  VCC: Bauteil1.VCC, Bauteil2.5V, RE1.Vcc
  N1: Bauteil1.SDA, Bauteil2.A4
  N2: Bauteil1.SCL, Bauteil2.A5
  N3: Bauteil2.D8, RE1.DT
  N4: Bauteil2.D9, RE1.CLK

custom parts:
  LCD1602-I2C: A standard character display, usually with 2x16 characters. Comes in many colors with LCM1602 IIC attached.
  KY-040 Rotary encoder: KY-040 Rotary Encoder with switch on breakout borad from AZ Delivery
